# Fritzing sketch fibonacci (saved by Fritzing 0.9.2b)
circuit board: 8cm x 6.5cm
breadboards: 2

parts:
  ATMEGA_328P = atmega328 [package=dip]
  7805 = Voltage Regulator - 5V [package="TO220 [THT]"]
  6-12V = Power plug
  C1 = Ceramic Capacitor [capacitance=100nF package="100 mil [THT, multilayer]"]
  C2 = Electrolytic Capacitor [capacitance=0.1mF package="100 mil [THT, electrolytic]"]
  C3 = Electrolytic Capacitor [capacitance=10µF package="100 mil [THT, electrolytic]"]
  R1 = Resistor [tolerance=±5% resistance=220 package=THT]
  PWR = LED - 3mm [color="Green (560nm)" package="3 mm [THT]"]
  R2 = Resistor [tolerance=±5% resistance=10k package=THT]
  16MHz = Crystal [frequency="16 Mhz" package=THT]
  C4 = Ceramic Capacitor [capacitance=100nF package="100 mil [THT, multilayer]"]
  C5 = Ceramic Capacitor [capacitance=22pF package="100 mil [THT, multilayer]"]
  C6 = Ceramic Capacitor [capacitance=22pF package="100 mil [THT, multilayer]"]
  R3 = Resistor [tolerance=±5% resistance=220 package=THT]
  #13 = LED - 3mm [color="Yellow (595nm)" package="3 mm [THT]"]
  DS1307 = DS1307 [package=THT]
  R4 = Resistor [tolerance=±5% resistance=2.2k package=THT]
  R5 = Resistor [tolerance=±5% resistance=2.2k package=THT]
  32kHz = CRYSTAL - kHz [frequency="32 kHz"]
  LEDs = screw terminal, 3 pins
  R6 = Resistor [tolerance=±5% resistance=10k package=THT]
  R7 = Resistor [tolerance=±5% resistance=10k package=THT]
  R8 = Resistor [tolerance=±5% resistance=10k package=THT]
  R9 = Resistor [tolerance=±5% resistance=10k package=THT]
  S1 = SWITCH-MOMENTARY-2 [package=tactile-pth-12mm]
  S2 = SWITCH-MOMENTARY-2 [package=tactile-pth-12mm]
  S3 = SWITCH-MOMENTARY-2 [package=tactile-pth-12mm]
  S4 = SWITCH-MOMENTARY-2 [package=tactile-pth-12mm]
  CR1220 = Battery Holders [package=battcon_12mm_pth]
  S5 = Pushbutton [package="[THT]"]
  C7 = Ceramic Capacitor [capacitance=100nF package="100 mil [THT, multilayer]"]
  FTDI = male pin header, 6 pins [form="♂ (male)"]

nets:
  N1: ATMEGA_328P.RESET, R2.Pin_0, S5.Pin_1, S5.Pin_2, C7.0
  N2: ATMEGA_328P.D0_(RX), FTDI.pin3
  N3: ATMEGA_328P.D1_(TX), FTDI.pin2
  N4: ATMEGA_328P.D3_(PWM), R9.Pin_0, S3.1
  N5: ATMEGA_328P.D4, R8.Pin_0, S2.1
  N6: ATMEGA_328P.VCC, 7805.output_voltage, C3.+, R1.Pin_1, R2.Pin_1, C4.0, DS1307.+V, R4.Pin_0, R5.Pin_0, LEDs.pin1, S1.2, S2.2, S3.2, S4.2, FTDI.pin4
  GND: ATMEGA_328P.GND#7, 7805.GND, 6-12V.GND, C1.1, C2.-, C3.-, PWR.cathode, C4.1, C5.1, C6.0, R3.Pin_1, DS1307.0V, LEDs.pin3, R6.Pin_1, R7.Pin_1, R8.Pin_1, R9.Pin_1, CR1220.-, S5.Pin_3, S5.Pin_4, FTDI.pin5, FTDI.pin6
  N7: ATMEGA_328P.XLAT1, 16MHz.pin_0, C6.1
  N8: ATMEGA_328P.XLAT2, 16MHz.pin_1, C5.0
  N9: ATMEGA_328P.D5_(PWM), R7.Pin_0, S4.1
  N10: ATMEGA_328P.D6_(PWM), R6.Pin_0, S1.1
  N11: ATMEGA_328P.D8, LEDs.pin2
  N12: ATMEGA_328P.D13, #13.anode
  N13: ATMEGA_328P.A4, DS1307.SDA_-_I2C_Data, R4.Pin_1
  N14: ATMEGA_328P.A5, DS1307.SCL_-_I2C_Clock, R5.Pin_1
  N15: 7805.input_voltage, 6-12V.VCC, C1.0, C2.+
  N16: R1.Pin_0, PWR.anode
  N17: R3.Pin_0, #13.cathode
  N18: DS1307.X1_-_Crystal, 32kHz.pin_0
  N19: DS1307.X2_-_Crystal, 32kHz.pin_1
  N20: DS1307.Vbat_-_Backup_Supply, CR1220.+
  N21: C7.1, FTDI.pin1

notes:
  +
  BASBRUN.COM
  Fibonacci Clock v1.2
